# Fritzing sketch hoermi (saved by Fritzing 0.9.5d)
breadboards: 1

parts:
  Part1 = Arduino Uno (Rev3)
  Grove1 = Grove OLED 128x96
  ZS-042_RTC1 = ZS-042 RTC Module
  DS1 = DS18B20 1-Wire Temperature Sensor [part_number=DS18B20]
  DS2 = DS18B20 1-Wire Temperature Sensor [part_number=DS18B20]

nets:
  N1: Part1.A4/SDA, Grove1.SDA, ZS-042_RTC1.SDA
  N2: Part1.A5/SCL, Grove1.SCL, ZS-042_RTC1.SCL
  VCC: Part1.D4, Part1.5V, Grove1.VCC, ZS-042_RTC1.VCC, DS1.DQ, DS1.VDD, DS2.DQ, DS2.VDD
  GND: Part1.GND, Grove1.GND, ZS-042_RTC1.GND, DS1.GND, DS2.GND
